# Fritzing sketch watering (saved by Fritzing 0.9.9b)
circuit board: 8.46667cm x 5.64444cm
breadboards: 1

parts:
  WeMos_D1_Mini1 = WeMos D1 Mini
  water_tank_level_sensor = HC-SR04 Ultrasonic Distance Sensor
  pump_relay = KY-019 5V Relay Module [package="Breakout board"]
  Bauteil2 = FC-28 Soil Hygrometer Module
  soil_sensor = FC-28 Soil Hygrometer Module - Probe
  PUMP = DC Motor
  J1 = Power Jack [package=power_jack_pth]
  V1 = DC Power [voltage=5]

nets:
  VCC: WeMos_D1_Mini1.5V, water_tank_level_sensor.VCC, pump_relay.+, Bauteil2.VCC, J1.PWR
  N1: WeMos_D1_Mini1.D5, water_tank_level_sensor.ECHO
  N2: WeMos_D1_Mini1.D6, water_tank_level_sensor.TRIG
  GND: WeMos_D1_Mini1.G, water_tank_level_sensor.GND, pump_relay.-, Bauteil2.GND, J1.GND
  N3: pump_relay.Common, PUMP.pin_1
  N4: Bauteil2.POS, soil_sensor.POS
  N5: Bauteil2.NEG, soil_sensor.NEG
  N6: PUMP.pin_2, V1.V-

custom parts:
  KY-019 5V Relay Module: KY-019 5V Relay module, used to control AC circuits. (Special thanks to vanepp for fixing the PCB holes and other errors)
  FC-28 Soil Hygrometer Module: The FC-28 is a soil hygrometer module that uses the Texas Instruments LM393 comparator chip to provide an analog measurement of soil humidity. The digital output is high when soil moisture is over a certain threshold, as determined by adjusting the potentiometer.
  FC-28 Soil Hygrometer Module - Probe: The FC-28 is a soil hygrometer module that uses the Texas Instruments LM393 comparator chip to provide an analog measurement of soil humidity.
